// Logisim project Practice_2.circ as structural Verilog: 3 circuits, main circuit main
module main (
  output out_1,
  output out_2
);

  wire and_1_out, and_2_out, and_3_out, clock_1_out, counter_1_carry, t_ff_1_q, \сднф_1_out_6 ,
       \скнф_1_out_6 ;
  wire [4:0] counter_1_q;
  wire [31:0] shift_register_1_q0, shift_register_2_q0;

  Counter #(.width(5), .max('h1f)) counter_1 (
    .Q(counter_1_q), .carry(counter_1_carry), .clk(and_1_out));  // open: load, D, count, clr
  and and_1 (and_1_out, clock_1_out, ~counter_1_carry);  // AND_Gate
  Clock clock_1 (.out(clock_1_out));
  and and_2 (and_2_out, ~t_ff_1_q, counter_1_carry);  // AND_Gate
  T_Flip_Flop t_ff_1 (.clk(clock_1_out), .T(and_2_out), .Q(t_ff_1_q));  // open: Qn, preset, reset, en
  \СДНФ  \u_сднф_1  (
    ._1(counter_1_q[4]), ._2(counter_1_q[3]), ._3(counter_1_q[2]), ._4(counter_1_q[1]),
    ._1_2(counter_1_q[0]), .out_6(\сднф_1_out_6 ));
  Shift_Register #(.length(32)) shift_register_1 (
    .in(\сднф_1_out_6 ), .clk(and_3_out), .q0(shift_register_1_q0[0]), .q1(shift_register_1_q0[1]),
    .q2(shift_register_1_q0[2]), .q3(shift_register_1_q0[3]), .q4(shift_register_1_q0[4]),
    .q5(shift_register_1_q0[5]), .q6(shift_register_1_q0[6]), .q7(shift_register_1_q0[7]),
    .q8(shift_register_1_q0[8]), .q9(shift_register_1_q0[9]), .q10(shift_register_1_q0[10]),
    .q11(shift_register_1_q0[11]), .q12(shift_register_1_q0[12]), .q13(shift_register_1_q0[13]),
    .q14(shift_register_1_q0[14]), .q15(shift_register_1_q0[15]), .q16(shift_register_1_q0[16]),
    .q17(shift_register_1_q0[17]), .q18(shift_register_1_q0[18]), .q19(shift_register_1_q0[19]),
    .q20(shift_register_1_q0[20]), .q21(shift_register_1_q0[21]), .q22(shift_register_1_q0[22]),
    .q23(shift_register_1_q0[23]), .q24(shift_register_1_q0[24]), .q25(shift_register_1_q0[25]),
    .q26(shift_register_1_q0[26]), .q27(shift_register_1_q0[27]), .q28(shift_register_1_q0[28]),
    .q29(shift_register_1_q0[29]), .q30(shift_register_1_q0[30]), .q31(shift_register_1_q0[31]));  // open: shift, out, load, clr, d0, d1, d2, d3, d4, d5, d6, d7, d8, d9, d10, d11, d12, d13, d14, d15, d16, d17, d18, d19, d20, d21, d22, d23, d24, d25, d26, d27, d28, d29, d30, d31
  Shift_Register #(.length(32)) shift_register_2 (
    .in(\скнф_1_out_6 ), .clk(and_3_out), .q0(shift_register_2_q0[0]), .q1(shift_register_2_q0[1]),
    .q2(shift_register_2_q0[2]), .q3(shift_register_2_q0[3]), .q4(shift_register_2_q0[4]),
    .q5(shift_register_2_q0[5]), .q6(shift_register_2_q0[6]), .q7(shift_register_2_q0[7]),
    .q8(shift_register_2_q0[8]), .q9(shift_register_2_q0[9]), .q10(shift_register_2_q0[10]),
    .q11(shift_register_2_q0[11]), .q12(shift_register_2_q0[12]), .q13(shift_register_2_q0[13]),
    .q14(shift_register_2_q0[14]), .q15(shift_register_2_q0[15]), .q16(shift_register_2_q0[16]),
    .q17(shift_register_2_q0[17]), .q18(shift_register_2_q0[18]), .q19(shift_register_2_q0[19]),
    .q20(shift_register_2_q0[20]), .q21(shift_register_2_q0[21]), .q22(shift_register_2_q0[22]),
    .q23(shift_register_2_q0[23]), .q24(shift_register_2_q0[24]), .q25(shift_register_2_q0[25]),
    .q26(shift_register_2_q0[26]), .q27(shift_register_2_q0[27]), .q28(shift_register_2_q0[28]),
    .q29(shift_register_2_q0[29]), .q30(shift_register_2_q0[30]), .q31(shift_register_2_q0[31]));  // open: shift, out, load, clr, d0, d1, d2, d3, d4, d5, d6, d7, d8, d9, d10, d11, d12, d13, d14, d15, d16, d17, d18, d19, d20, d21, d22, d23, d24, d25, d26, d27, d28, d29, d30, d31
  \СКНФ  \u_скнф_1  (
    ._1(counter_1_q[4]), ._2(counter_1_q[3]), ._3(counter_1_q[2]), ._4(counter_1_q[1]),
    ._1_2(counter_1_q[0]), .out_6(\скнф_1_out_6 ));
  and and_3 (and_3_out, clock_1_out, ~t_ff_1_q);  // AND_Gate
  Comparator #(.width(32)) comparator_1 (.a(shift_register_1_q0), .b(32'h52263ecd), .eq(out_1));  // open: gt, lt
  Comparator #(.width(32)) comparator_2 (.a(shift_register_2_q0), .b(32'h52263ecd), .eq(out_2));  // open: gt, lt
endmodule

module \СДНФ  (
  input  _1,
  input  _2,
  input  _3,
  input  _4,
  input  _1_2,
  output out_6
);

  wire and_1_out, and_2_out, and_3_out, and_4_out, and_5_out, and_6_out, and_7_out, and_8_out, not_1_out,
       not_2_out, not_3_out, not_4_out, not_5_out;

  not not_1 (not_1_out, _2);
  not not_2 (not_2_out, _1);
  not not_3 (not_3_out, _4);
  not not_4 (not_4_out, _3);
  not not_5 (not_5_out, _1_2);
  and and_1 (and_1_out, _1, _2, not_3_out);
  and and_2 (and_2_out, _1, _3, not_3_out);
  and and_3 (and_3_out, _1, _2, _3, _1_2);
  and and_4 (and_4_out, _2, _3, not_3_out, _1_2);
  and and_5 (and_5_out, not_2_out, _2, _4, not_5_out);
  and and_6 (and_6_out, not_2_out, not_1_out, not_4_out, _1_2);
  and and_7 (and_7_out, _1, not_1_out, not_4_out, _4);
  and and_8 (and_8_out, not_1_out, _3, _4, not_5_out);
  or or_1 (out_6, and_8_out, and_7_out, and_6_out, and_5_out, and_4_out, and_3_out, and_2_out, and_1_out);

  // Notes on the sheet:
  //   5
  //   2
  //   3
  //   5
  //   4
endmodule

module \СКНФ  (
  input  _1,
  input  _2,
  input  _3,
  input  _4,
  input  _1_2,
  output out_6
);

  wire not_1_out, not_2_out, not_3_out, not_4_out, not_5_out, or_1_out, or_2_out, or_3_out, or_4_out,
       or_5_out, or_6_out, or_7_out, or_8_out, or_9_out;

  not not_1 (not_1_out, _1);
  not not_2 (not_2_out, _2);
  not not_3 (not_3_out, _1_2);
  not not_4 (not_4_out, _4);
  not not_5 (not_5_out, _3);
  or or_1 (or_1_out, _1, _4, _1_2);
  or or_2 (or_2_out, not_1_out, _2, _3, _4);
  or or_3 (or_3_out, _1, _2, _3, _1_2);
  or or_4 (or_4_out, not_1_out, not_2_out, not_4_out, _1_2);
  or or_5 (or_5_out, _2, not_5_out, not_4_out, not_3_out);
  or or_6 (or_6_out, not_1_out, not_2_out, _3, not_4_out);
  or or_7 (or_7_out, _1, not_2_out, _3, _4);
  or or_8 (or_8_out, _1, not_2_out, not_4_out, not_3_out);
  or or_9 (or_9_out, _1, _2, not_5_out, _4);
  and and_1 (out_6, or_9_out, or_8_out, or_7_out, or_6_out, or_5_out, or_4_out, or_3_out, or_2_out, or_1_out);

  // Notes on the sheet:
  //   5
  //   3
  //   2
  //   4
  //   5
endmodule
